# Fritzing sketch raspberry closed-loop stepper   (saved by Fritzing 0.9.10b)
circuit board: 8.53488cm x 5.63626cm
breadboards: 1

parts:
  ENC_1 = Camdenboss CTB0158-4 [part_number=CTB0158-4 package=THT]
  LSW1 = Camdenboss CTB0158-2 [part_number=CTB0158-2 package=THT]
  LSW2 = Camdenboss CTB0158-2 [part_number=CTB0158-2 package=THT]
  STP_DRV = Camdenboss CTB0158-4 [part_number=CTB0158-4 package=THT]
  S1 = Pushbutton [package="[THT]"]
  N2048 = Raspberry Pi 3 [part_number=RPI-3-V1.2]
  S2 = Pushbutton [package="[THT]"]

nets:
  GND: ENC_1.pin1, LSW1.pin1, LSW2.pin1, STP_DRV.pin1, S1.Pin_3, S1.Pin_4, N2048.GND, S2.Pin_3
  5V/VCC: ENC_1.pin2, N2048.5V
  ENCB: ENC_1.pin3, N2048.GPIO26
  ENCA: ENC_1.pin4, N2048.GPIO19
  LSW1: LSW1.pin2, N2048.GPIO27
  LSW2: LSW2.pin2, N2048.GPIO22
  PUL: STP_DRV.pin2, N2048.GPIO13
  DIR: STP_DRV.pin3, N2048.GPIO6
  ENA: STP_DRV.pin4, N2048.GPIO5
  BTN1: S1.Pin_1, S1.Pin_2, N2048.GPIO4
  BTN2: N2048.GPIO17, S2.Pin_1

notes:
  A
  B
  VCC
  GND
  PUL
  DIR
  ENA

// code stored in the sketch: raspberry closed-loop stepper  .ino

